// Logisim project PipelinedCoreEV.circ as structural Verilog
module RVI1cycle (
);

  wire aluabstraction_1_branch, ALUSrc, ALUSrcID, Branch, branchalu_1_branchaluoutput, BranchID, clk,
       exmem_1_memtoreg, exmem_1_zero, idex_1_out_19, idex_1_out_20, idex_1_out_22, idex_1_out_24, IFIDFlush,
       IFIDWrite, maincontrol_1_memwrite, maincontrol_1_regwrite, MemRead, MemReadEX, MemReadID, MemtoReg,
       MemtoRegID, MemWrite, MemWriteID, or_1_out, PCSrc, PCWrite, RegWrite, RegWriteID, RegWriteMEM, rst,
       Stall;
  wire [1:0] ForwardALUA, ForwardALUB, forwarding_1_forwarda, forwarding_1_forwardb;
  wire [4:0] ALUCtrl, ALUCtrlID, EXRd, EXRs1, EXRs2, MEMRd, Rs1, Rs2, WBRd;
  wire [7:0] undriven_2;
  wire [31:0] adder_1_out, adder_2_out, aluabstraction_1_aluoutput, exmem_1_out_20, exmem_1_pcbranch,
       idex_1_immediate, idex_1_out_18, idex_1_out_23, idex_1_out_27, idex_1_readdata1, ifid_1_instruction,
       ifid_1_out_6, Immediate, memwb_1_dataoutput, memwb_1_out_8, MEMWriteData, multiplexer_1_out,
       multiplexer_2_out, multiplexer_5_out, multiplexer_6_out, multiplexer_7_out, ReadData1, ReadData2,
       undriven, undriven_3, undriven_4, undriven_5, WriteData;

  Clock u_clk (.out(clk));
  Button ResetRegs (.out(rst));
  ROM #(.dataWidth(32)) rom_1 ();  // open: addr, data
  Multiplexer #(.width(32)) multiplexer_1 (.in0(adder_1_out), .in1(adder_2_out), .out(multiplexer_1_out), .sel(PCSrc));
  Adder #(.width(32)) adder_1 (
    .a(32'h4), .b({undriven[31:10], undriven_2, undriven[1:0]}), .out(adder_1_out));  // open: cin, cout
  Register #(.width(32)) PC ();  // open: D, en, clk, Q, clr
  IFID ifid_1 (
    .out_6(ifid_1_out_6), .Instruction({ifid_1_instruction[31:25], Rs2, Rs1, ifid_1_instruction[14:0]}),
    .clk(clk), .rst(or_1_out), .en(IFIDWrite), .PC({undriven[31:10], undriven_2, undriven[1:0]}),
    .in_5(undriven_3));
  or or_1 (or_1_out, IFIDFlush, rst);
  // Probe on {ifid_1_instruction[31:25], Rs2, Rs1, ifid_1_instruction[14:0]}
  MainControl maincontrol_1 (
    .ALUSrc(ALUSrcID), .MemtoReg(MemtoRegID), .RegWrite(maincontrol_1_regwrite), .MemRead(MemReadID),
    .MemWrite(maincontrol_1_memwrite), .Branch(BranchID), .ALUCtrl(ALUCtrlID),
    .Instruction({ifid_1_instruction[31:25], Rs2, Rs1, ifid_1_instruction[14:0]}));
  ImmGen immgen_1 (
    .Immediate(Immediate), .Instruction({ifid_1_instruction[31:25], Rs2, Rs1, ifid_1_instruction[14:0]}));
  Forwarding forwarding_1 (
    .ForwardA(forwarding_1_forwarda), .ForwardB(forwarding_1_forwardb), .RegWriteMEM(RegWriteMEM),
    .RegWrite(RegWrite), .ALUSrc(ALUSrc), .MEMRd(MEMRd), .WBRd(WBRd), .Rs1(Rs1), .Rs2(Rs2));
  Multiplexer #(.select(2), .width(32)) multiplexer_2 (
    .in0(ReadData1), .in1(MEMWriteData), .in2(WriteData), .out(multiplexer_2_out), .sel(forwarding_1_forwarda));  // open: in3
  Multiplexer multiplexer_3 (.in0(maincontrol_1_regwrite), .in1(1'b0), .out(RegWriteID), .sel(Stall));
  Multiplexer multiplexer_4 (.in0(maincontrol_1_memwrite), .in1(1'b0), .out(MemWriteID), .sel(Stall));
  // Probe on Immediate
  HazardDetection hazarddetection_1 (
    .PCWrite(PCWrite), .IFIDWrite(IFIDWrite), .Stall(Stall), .IFIDFlush(IFIDFlush),
    .Instruction({ifid_1_instruction[31:25], Rs2, Rs1, ifid_1_instruction[14:0]}), .MemReadID(MemReadID),
    .MemReadEX(MemReadEX), .BranchID(BranchID), .EXRd(EXRd), .PCSrc(PCSrc));
  Adder #(.width(32)) adder_2 (.a(ifid_1_out_6), .b(Immediate), .out(adder_2_out));  // open: cin, cout
  RegisterFile registerfile_1 (
    .ReadData1(ReadData1), .ReadData2(ReadData2), .Rs1(Rs1), .Rs2(Rs2), .Rd(WBRd), .clk(clk), .rst(rst),
    .WriteData(WriteData), .WriteEn(RegWrite));
  // Probe on ReadData1
  // Probe on ReadData2
  Multiplexer #(.select(2), .width(32)) multiplexer_5 (
    .in0(ReadData2), .in1(MEMWriteData), .in2(WriteData), .in3(undriven_4), .out(multiplexer_5_out),
    .sel(forwarding_1_forwardb));
  BranchALU branchalu_1 (
    .BranchALUOutput(branchalu_1_branchaluoutput), .BranchA(multiplexer_2_out), .BranchB(multiplexer_5_out),
    .ALUCtrl(ALUCtrlID));
  and and_1 (PCSrc, branchalu_1_branchaluoutput, BranchID);
  IDEX idex_1 (
    .out_19(idex_1_out_19), .out_20(idex_1_out_20), .out_22(idex_1_out_22), .out_24(idex_1_out_24),
    .MemRead(MemReadEX), .out_28(ALUSrc), .ALUOp(ALUCtrl), .ReadDir1(EXRs1), .ReadDir2(EXRs2),
    .out_18(idex_1_out_18), .ReadData1(idex_1_readdata1), .out_23(idex_1_out_23),
    .Immediate(idex_1_immediate), .out_27(idex_1_out_27), .out_29(EXRd), .clk(clk), .rst(rst), .in_16(Rs1),
    .in_17(Rs2), .PC(ifid_1_out_6), .in_6(ReadData1), .ReadData2(ReadData2), .in_10(Immediate),
    .Instruction({ifid_1_instruction[31:25], Rs2, Rs1, ifid_1_instruction[14:0]}),
    .Rd(ifid_1_instruction[11:7]), .RegWrite(RegWriteID), .MemtoReg(MemtoRegID), .Branch(BranchID),
    .MemWrite(MemWriteID), .in_11(MemReadID), .ALUSrc(ALUSrcID), .in_15(ALUCtrlID));
  // Probe on idex_1_out_23
  Forwarding forwarding_2 (
    .ForwardA(ForwardALUA), .ForwardB(ForwardALUB), .RegWriteMEM(RegWriteMEM), .RegWrite(RegWrite),
    .ALUSrc(ALUSrc), .MEMRd(MEMRd), .WBRd(WBRd), .Rs1(EXRs1), .Rs2(EXRs2));
  // Probe on multiplexer_6_out
  Multiplexer #(.select(2), .width(32)) multiplexer_6 (
    .in0(idex_1_readdata1), .in1(MEMWriteData), .in2(WriteData), .out(multiplexer_6_out), .sel(ForwardALUA));  // open: in3
  Multiplexer #(.select(2), .width(32)) multiplexer_7 (
    .in0(idex_1_out_23), .in1(MEMWriteData), .in2(WriteData), .in3(idex_1_immediate),
    .out(multiplexer_7_out), .sel(ForwardALUB));
  // Probe on multiplexer_7_out
  ALUAbstraction aluabstraction_1 (
    .ALUOutput(aluabstraction_1_aluoutput), .Branch(aluabstraction_1_branch), .ALUA(multiplexer_6_out),
    .ALUCtrl(ALUCtrl), .ALUB(multiplexer_7_out));
  EXMEM exmem_1 (
    .RegWrite(RegWriteMEM), .MemtoReg(exmem_1_memtoreg), .out_18(Branch), .MemWrite(MemWrite),
    .out_21(MemRead), .PCBranch(exmem_1_pcbranch), .out_17(MEMWriteData), .out_20(exmem_1_out_20),
    .Rd(MEMRd), .Zero(exmem_1_zero), .clk(clk), .rst(rst), .in_6(aluabstraction_1_branch),
    .ALUOutput(aluabstraction_1_aluoutput), .ReadData2(idex_1_out_23), .in_12(EXRd), .in_4(idex_1_out_19),
    .in_5(idex_1_out_20), .Branch(idex_1_out_22), .in_9(idex_1_out_24), .MemRead(MemReadEX));  // open: in_3
  RAM #(.dataWidth(32)) ram_1 ();  // open: addr, we, oe, clk, din, dout
  // Probe on MEMWriteData
  // Probe on undriven_5
  MEMWB memwb_1 (
    .RegWrite(RegWrite), .out_10(MemtoReg), .out_8(memwb_1_out_8), .DataOutput(memwb_1_dataoutput),
    .WriteDir(WBRd), .clk(clk), .rst(rst), .ALUOutput(MEMWriteData), .in_6(undriven_5), .in_7(MEMRd),
    .in_4(RegWriteMEM), .MemtoReg(exmem_1_memtoreg));
  Multiplexer #(.width(32)) multiplexer_8 (
    .in0(memwb_1_out_8), .in1(memwb_1_dataoutput), .out(WriteData), .sel(MemtoReg));
  // Probe on WriteData

  // Notes on the sheet:
  //   contents of rom_1 (hex, n*v repeats v):
  //   52503 45a583 a58633 c2a223 2b60063 40b606b3 40d60633 b60a63 4*0 c6f6b3 c6e733
  //   PCNext
  //   PCPlus4
  //   PC
  //   Alineado a word (1:0 = 0)
  //   Instruction
  //   IFIDRst
  //   IDPC
  //   IDInstruction
  //   Stall
  //   Flush
  //   ForwardBranchA
  //   Immediate
  //   Rd
  //   Instruction (Rs1, Rs2, Opcode)
  //   Moved Equality test (Branch calculation) from EX to ID
  //   ForwardBranchB
  //   BranchA
  //   Instruction
  //   BranchB
  //   PC
  //   EXReadData1
  //   EXReadData2
  //   EXImmediate
  //   Datapath: No Pipeline Identificator means the signal is created in that segment
  //   Pipeline Identificator placed before name
  //   Control: No Pipeline Identificator means signal is used in that segment
  //   Pipeline Identificator placed after name
  //   ALUA
  //   ALUB
  //   PC
  //   Branch
  //   ALUBranch
  //   ALUOutput
  //   MEMALUOutput
  //   Branching moved to ID stage
  //   Reduce cost of missprediction
  //   MEMRead or RegWrite -> LOAD
  //   Alineado a word (1:0 = 0)
  //   ALUOutput
  //   DataOutput
  //   WriteData
endmodule

module MainControl (
  input  [31:0] Instruction,
  output ALUSrc,
  output MemtoReg,
  output RegWrite,
  output MemRead,
  output MemWrite,
  output Branch,
  output [4:0] ALUCtrl
);

  wire lw_out, or_1_out, or_2_out, sw_out;
  wire [1:0] beq_out;
  wire [6:0] undriven;

  and R (beq_out[1], ~undriven[6], undriven[5], undriven[4], ~undriven[3], ~undriven[2], undriven[1], undriven[0]);  // AND_Gate
  and lw (lw_out, ~undriven[6], ~undriven[5], ~undriven[4], ~undriven[3], ~undriven[2], undriven[1], undriven[0]);  // AND_Gate
  and sw (sw_out, ~undriven[6], undriven[5], ~undriven[4], ~undriven[3], ~undriven[2], undriven[1], undriven[0]);  // AND_Gate
  and beq (beq_out[0], undriven[6], undriven[5], ~undriven[4], ~undriven[3], ~undriven[2], undriven[1], undriven[0]);  // AND_Gate
  or or_1 (or_1_out, lw_out, sw_out);
  or or_2 (or_2_out, beq_out[1], lw_out);

  // Notes on the sheet:
  //   Opcode
  //   func3
  //   func7
endmodule

module RegisterFile (
  input  [4:0] Rs1,
  input  [4:0] Rs2,
  input  WriteEn,
  input  [4:0] Rd,
  input  [31:0] WriteData,
  input  clk,
  input  rst,
  output [31:0] ReadData1,
  output [31:0] ReadData2
);

  wire [15:0] decoder_1_out0, decoder_1_out16;
  wire [31:0] x1ra_q, x2sp_p6, x2sp_p7, x2sp_p8, x3gp_p8, x4tp_p8, x5t0_p8, x6t1_p8, x7t2_p8, x8s0fp_p8,
       x9s1_p8, x10a0_p8, x11a1_p8, x12a2_p8, x13a3_p8, x16a6_q, x17a7_p6, x17a7_p7, x17a7_p8, x17a7_p9,
       x19s3_p7, x20s4_p8, x21s5_p8, x22s6_p8, x23s7_p8, x24s8_p8, x25s9_p8, x26s10_p8, x27s11_p8, x28t3_p8,
       x29t4_p8;

  Decoder #(.select(5)) decoder_1 (
    .out0(decoder_1_out0[0]), .out1(decoder_1_out0[1]), .out2(decoder_1_out0[2]), .out3(decoder_1_out0[3]),
    .out4(decoder_1_out0[4]), .out5(decoder_1_out0[5]), .out6(decoder_1_out0[6]), .out7(decoder_1_out0[7]),
    .out8(decoder_1_out0[8]), .out9(decoder_1_out0[9]), .out10(decoder_1_out0[10]),
    .out11(decoder_1_out0[11]), .out12(decoder_1_out0[12]), .out13(decoder_1_out0[13]),
    .out14(decoder_1_out0[14]), .out15(decoder_1_out0[15]), .out16(decoder_1_out16[0]),
    .out17(decoder_1_out16[1]), .out18(decoder_1_out16[2]), .out19(decoder_1_out16[3]),
    .out20(decoder_1_out16[4]), .out21(decoder_1_out16[5]), .out22(decoder_1_out16[6]),
    .out23(decoder_1_out16[7]), .out24(decoder_1_out16[8]), .out25(decoder_1_out16[9]),
    .out26(decoder_1_out16[10]), .out27(decoder_1_out16[11]), .out28(decoder_1_out16[12]),
    .out29(decoder_1_out16[13]), .out30(decoder_1_out16[14]), .out31(decoder_1_out16[15]), .sel(Rd),
    .en(WriteEn));
  // Probe on decoder_1_out0
  // Probe on Rd
  Register #(.width(32)) x1ra (.D(WriteData), .en(decoder_1_out0[1]), .Q(x1ra_q), .clk(clk), .clr(rst));
  // Register #(.width(32)) x2sp: pin names not known; wires that end beside it: WriteData, decoder_1_out0[2], WriteData, decoder_1_out0[3], WriteData, x2sp_p6, x2sp_p7, x2sp_p8
  // Register #(.width(32)) x3gp: pin names not known; wires that end beside it: WriteData, decoder_1_out0[3], WriteData, decoder_1_out0[4], WriteData, x2sp_p7, x2sp_p8, x3gp_p8
  // Register #(.width(32)) x4tp: pin names not known; wires that end beside it: WriteData, decoder_1_out0[4], WriteData, decoder_1_out0[5], WriteData, x2sp_p8, x3gp_p8, x4tp_p8
  // Register #(.width(32)) x5t0: pin names not known; wires that end beside it: WriteData, decoder_1_out0[5], WriteData, decoder_1_out0[6], WriteData, x3gp_p8, x4tp_p8, x5t0_p8
  // Register #(.width(32)) x6t1: pin names not known; wires that end beside it: WriteData, decoder_1_out0[6], WriteData, decoder_1_out0[7], WriteData, x4tp_p8, x5t0_p8, x6t1_p8
  // Register #(.width(32)) x7t2: pin names not known; wires that end beside it: WriteData, decoder_1_out0[7], WriteData, decoder_1_out0[8], WriteData, x5t0_p8, x6t1_p8, x7t2_p8
  // Register #(.width(32)) x8s0fp: pin names not known; wires that end beside it: WriteData, decoder_1_out0[8], WriteData, decoder_1_out0[9], WriteData, x6t1_p8, x7t2_p8, x8s0fp_p8
  // Register #(.width(32)) x9s1: pin names not known; wires that end beside it: WriteData, decoder_1_out0[9], WriteData, decoder_1_out0[10], WriteData, x7t2_p8, x8s0fp_p8, x9s1_p8
  // Register #(.width(32)) x10a0: pin names not known; wires that end beside it: WriteData, decoder_1_out0[10], WriteData, decoder_1_out0[11], WriteData, x8s0fp_p8, x9s1_p8, x10a0_p8
  // Register #(.width(32)) x11a1: pin names not known; wires that end beside it: WriteData, decoder_1_out0[11], WriteData, decoder_1_out0[12], WriteData, x9s1_p8, x10a0_p8, x11a1_p8
  // Register #(.width(32)) x12a2: pin names not known; wires that end beside it: WriteData, decoder_1_out0[12], WriteData, decoder_1_out0[13], WriteData, x10a0_p8, x11a1_p8, x12a2_p8
  // Register #(.width(32)) x13a3: pin names not known; wires that end beside it: WriteData, decoder_1_out0[13], WriteData, decoder_1_out0[14], WriteData, x11a1_p8, x12a2_p8, x13a3_p8
  // Register #(.width(32)) x14a4: pin names not known; wires that end beside it: WriteData, decoder_1_out0[14], WriteData, decoder_1_out0[15], x12a2_p8, x13a3_p8
  // Register #(.width(32)) x15a5: pin names not known; wires that end beside it: WriteData, decoder_1_out0[15], x13a3_p8, clk
  // Probe on x11a1_p8
  Register #(.width(32)) x16a6 (.D(WriteData), .en(decoder_1_out16[0]), .Q(x16a6_q), .clk(clk), .clr(rst));
  // Register #(.width(32)) x17a7: pin names not known; wires that end beside it: WriteData, decoder_1_out16[1], WriteData, decoder_1_out16[2], WriteData, x17a7_p6, x17a7_p7, x17a7_p8, x17a7_p9
  // Register #(.width(32)) x18s2: pin names not known; wires that end beside it: WriteData, decoder_1_out16[2], WriteData, decoder_1_out16[3], WriteData, x17a7_p7, x17a7_p8, x17a7_p9
  // Register #(.width(32)) x19s3: pin names not known; wires that end beside it: WriteData, decoder_1_out16[3], WriteData, decoder_1_out16[4], WriteData, x17a7_p8, x19s3_p7, x17a7_p9
  // Register #(.width(32)) x20s4: pin names not known; wires that end beside it: WriteData, decoder_1_out16[4], WriteData, decoder_1_out16[5], WriteData, x17a7_p9, x19s3_p7, x20s4_p8
  // Register #(.width(32)) x21s5: pin names not known; wires that end beside it: WriteData, decoder_1_out16[5], WriteData, decoder_1_out16[6], WriteData, x19s3_p7, x20s4_p8, x21s5_p8
  // Register #(.width(32)) x22s6: pin names not known; wires that end beside it: WriteData, decoder_1_out16[6], WriteData, decoder_1_out16[7], WriteData, x20s4_p8, x21s5_p8, x22s6_p8
  // Register #(.width(32)) x23s7: pin names not known; wires that end beside it: WriteData, decoder_1_out16[7], WriteData, decoder_1_out16[8], WriteData, x21s5_p8, x22s6_p8, x23s7_p8
  // Register #(.width(32)) x24s8: pin names not known; wires that end beside it: WriteData, decoder_1_out16[8], WriteData, decoder_1_out16[9], WriteData, x22s6_p8, x23s7_p8, x24s8_p8
  // Register #(.width(32)) x25s9: pin names not known; wires that end beside it: WriteData, decoder_1_out16[9], WriteData, decoder_1_out16[10], WriteData, x23s7_p8, x24s8_p8, x25s9_p8
  // Register #(.width(32)) x26s10: pin names not known; wires that end beside it: WriteData, decoder_1_out16[10], WriteData, decoder_1_out16[11], WriteData, x24s8_p8, x25s9_p8, x26s10_p8
  // Register #(.width(32)) x27s11: pin names not known; wires that end beside it: WriteData, decoder_1_out16[11], WriteData, decoder_1_out16[12], WriteData, x25s9_p8, x26s10_p8, x27s11_p8
  // Register #(.width(32)) x28t3: pin names not known; wires that end beside it: WriteData, decoder_1_out16[12], WriteData, decoder_1_out16[13], WriteData, x26s10_p8, x27s11_p8, x28t3_p8
  // Register #(.width(32)) x29t4: pin names not known; wires that end beside it: WriteData, decoder_1_out16[13], WriteData, decoder_1_out16[14], WriteData, x27s11_p8, x28t3_p8, x29t4_p8
  // Register #(.width(32)) x30t5: pin names not known; wires that end beside it: WriteData, decoder_1_out16[14], WriteData, decoder_1_out16[15], x28t3_p8, x29t4_p8
  // Register #(.width(32)) x31t6: pin names not known; wires that end beside it: WriteData, decoder_1_out16[15], x29t4_p8
  Multiplexer #(.select(5), .width(32)) multiplexer_1 (
    .in0({32{1'b0}}), .in1(x1ra_q), .in2(x2sp_p6), .in3(x2sp_p7), .in4(x2sp_p8), .in5(x3gp_p8),
    .in6(x4tp_p8), .in7(x5t0_p8), .in8(x6t1_p8), .in9(x7t2_p8), .in10(x8s0fp_p8), .in11(x9s1_p8),
    .in12(x10a0_p8), .in13(x11a1_p8), .in14(x12a2_p8), .in15(x13a3_p8), .in16(x16a6_q), .in17(x17a7_p6),
    .in18(x17a7_p7), .in19(x17a7_p8), .in20(x17a7_p9), .in21(x19s3_p7), .in22(x20s4_p8), .in23(x21s5_p8),
    .in24(x22s6_p8), .in25(x23s7_p8), .in26(x24s8_p8), .in27(x25s9_p8), .in28(x26s10_p8), .in29(x27s11_p8),
    .in30(x28t3_p8), .in31(x29t4_p8), .out(ReadData1), .sel(Rs1));
  Multiplexer #(.select(5), .width(32)) multiplexer_2 (
    .in0({32{1'b0}}), .in1(x1ra_q), .in2(x2sp_p6), .in3(x2sp_p7), .in4(x2sp_p8), .in5(x3gp_p8),
    .in6(x4tp_p8), .in7(x5t0_p8), .in8(x6t1_p8), .in9(x7t2_p8), .in10(x8s0fp_p8), .in11(x9s1_p8),
    .in12(x10a0_p8), .in13(x11a1_p8), .in14(x12a2_p8), .in15(x13a3_p8), .in16(x16a6_q), .in17(x17a7_p6),
    .in18(x17a7_p7), .in19(x17a7_p8), .in20(x17a7_p9), .in21(x19s3_p7), .in22(x20s4_p8), .in23(x21s5_p8),
    .in24(x22s6_p8), .in25(x23s7_p8), .in26(x24s8_p8), .in27(x25s9_p8), .in28(x26s10_p8), .in29(x27s11_p8),
    .in30(x28t3_p8), .in31(x29t4_p8), .out(ReadData2), .sel(Rs2));

  // Notes on the sheet:
  //   WriteReg
  //   If not not-floating,
  //   when disabled, it can lead to
  //   write all regs
  //   x0zero
endmodule

module ALUAbstraction (
  input  [31:0] ALUA,
  input  [31:0] ALUB,
  input  [4:0] ALUCtrl,
  output [31:0] ALUOutput,
  output Branch
);

  wire comparator_3_gt, comparator_4_eq, comparator_4_lt;
  wire [0:0] beq, bge, bgeu, blt, bltu, bne, sltu;
  wire [31:0] add, \and , \or , sll, slt, sra, srl, sub, undriven, \xor ;

  Adder #(.width(32)) adder_1 (.a(ALUA), .b(ALUB), .out(add));  // open: cin, cout
  Subtractor #(.width(32)) subtractor_1 (.a(ALUA), .b(ALUB), .out(sub));  // open: bin, bout
  Shifter #(.width(32)) shifter_1 (.in(ALUA), .\dist (ALUB[4:0]), .out(sll));
  Comparator #(.width(32)) comparator_1 (.a(ALUA), .b(ALUB), .lt(slt[0]));  // open: gt, eq
  Comparator #(.mode("unsigned"), .width(32)) comparator_2 (.a(ALUA), .b(ALUB), .lt(sltu[0]));  // open: gt, eq
  assign \xor  = ALUA ^ ALUB;  // XOR_Gate xor_1, 32 bits wide
  Shifter #(.shift("lr"), .width(32)) shifter_2 (.in(ALUA), .\dist (ALUB[4:0]), .out(srl));
  Shifter #(.shift("ar"), .width(32)) shifter_3 (.in(ALUA), .\dist (ALUB[4:0]), .out(sra));
  assign \or  = ALUA | ALUB;  // OR_Gate or_1, 32 bits wide
  assign \and  = ALUA & ALUB;  // AND_Gate and_1, 32 bits wide
  Comparator #(.width(32)) comparator_3 (.a(ALUA), .b(ALUB), .gt(comparator_3_gt), .eq(beq[0]), .lt(blt[0]));
  Comparator #(.mode("unsigned"), .width(32)) comparator_4 (
    .a(ALUA), .b(ALUB), .gt(bltu[0]), .eq(comparator_4_eq), .lt(comparator_4_lt));
  not not_1 (bne[0], beq[0]);
  or or_2 (bge[0], comparator_3_gt, beq[0]);
  or or_3 (bgeu[0], bltu[0], comparator_4_eq);
  Multiplexer #(.select(5), .width(32)) multiplexer_1 (
    .in0(add), .in1(sub), .in2(sll), .in3(slt), .in4(undriven), .in5(\xor ), .in6(srl), .in7(sra),
    .in8(\or ), .in9(\and ), .out(ALUOutput), .sel(ALUCtrl));  // open: in10, in11, in12, in13, in14, in15, in16, in17, in18, in19, in20, in21, in22, in23, in24, in25, in26, in27, in28, in29, in30, in31

  assign Branch = ALUOutput[0];

  // Notes on the sheet:
  //   add, addi
  //   sub
  //   sll
  //   slt, slti
  //   sltu, sltiu
  //   xor, xori
  //   srl, srli
  //   sra, srai
  //   or, ori
  //   and, andi
  //   Signed
  //   Unsigned
  //   beq
  //   bne
  //   blt
  //   bge
  //   bltu
  //   bgeu
endmodule

module BranchALU (
  input  [31:0] BranchA,
  input  [31:0] BranchB,
  input  [4:0] ALUCtrl,
  output BranchALUOutput
);

  wire comparator_1_gt, comparator_2_eq, comparator_2_lt;
  wire [31:0] beq, bge, bgeu, blt, bltu, bne;
  wire [31:1] multiplexer_1_out;

  Comparator #(.width(32)) comparator_1 (.a(BranchA), .b(BranchB), .gt(comparator_1_gt), .eq(beq[0]), .lt(blt[0]));
  Comparator #(.mode("unsigned"), .width(32)) comparator_2 (
    .a(BranchA), .b(BranchB), .gt(bltu[0]), .eq(comparator_2_eq), .lt(comparator_2_lt));
  not not_1 (bne[0], beq[0]);
  or or_1 (bge[0], comparator_1_gt, beq[0]);
  or or_2 (bgeu[0], bltu[0], comparator_2_eq);
  Multiplexer #(.select(5), .width(32)) multiplexer_1 (
    .in26(beq), .in27(bne), .in28(blt), .in29(bge), .in30(bltu), .in31(bgeu),
    .out({multiplexer_1_out, BranchALUOutput}), .sel(ALUCtrl));  // open: in0, in1, in2, in3, in4, in5, in6, in7, in8, in9, in10, in11, in12, in13, in14, in15, in16, in17, in18, in19, in20, in21, in22, in23, in24, in25

  // Notes on the sheet:
  //   Signed
  //   Unsigned
  //   beq
  //   bne
  //   blt
  //   bge
  //   bltu
  //   bgeu
endmodule

module ImmGen (
  input  [31:0] Instruction,
  output [31:0] Immediate
);

  wire [31:0] bit_extender_1_out, Btype, Itype, Jtype, shifter_1_out, Stype;

  Bit_Extender #(.in_width(20), .out_width(32)) bit_extender_1 (.out(bit_extender_1_out));  // open: in
  Shifter #(.width(32)) shifter_1 (.in(bit_extender_1_out), .\dist (5'b01100), .out(shifter_1_out));
  assign Stype = {{20{Instruction[31]}}, {Instruction[31:25], Instruction[11:7]}};  // Bit_Extender bit_extender_2
  assign Btype = {{19{Instruction[31]}}, {Instruction[31], Instruction[7], Instruction[30:25], Instruction[11:8], 1'b0}};  // Bit_Extender bit_extender_3
  assign Jtype = {{11{Instruction[31]}}, {Instruction[31], Instruction[19:12], Instruction[20], Instruction[30:21], 1'b0}};  // Bit_Extender bit_extender_4
  assign Itype = {{20{Instruction[31]}}, Instruction[31:20]};  // Bit_Extender bit_extender_5
  // Probe on Stype
  // Probe on Btype
  // Probe on {Instruction[31:12], {12{1'b0}}}
  // Probe on Jtype
  // Probe on Itype
  Multiplexer #(.select(5), .width(32)) multiplexer_1 (
    .in0(Itype), .in3(Itype), .in4(Itype), .in5({Instruction[31:12], {12{1'b0}}}), .in8(Stype),
    .in13({Instruction[31:12], {12{1'b0}}}), .in24(Btype), .in25(Itype), .in27(Jtype), .in28(Itype),
    .out(Immediate), .sel(Instruction[6:2]));  // open: in1, in2, in6, in7, in9, in10, in11, in12, in14, in15, in16, in17, in18, in19, in20, in21, in22, in23, in26, in29, in30, in31
  // Probe on Instruction[6:2]

  // Other names for the same wires on the sheet: Utype[31:12] = Instruction[31:12]

  // Notes on the sheet:
  //   "Sign Extend" [19:0] = 0
  //   Calculate all posibilities of immediates and select one of them based on opcode
  //   Use control lines to implement what of the immediates is being to be generated
  //   From this 2 options the second one seems to increment the complexity of the desing while the first one don't implicitly reduces its performance
  //   Bits 2-6 of opcode
  //   Loads
  //   fence
  //   Arithmetics
  //   aupic
  //   Stores
  //   lui
  //   Branches
  //   jalr
  //   jal
  //   ecall/ebreak
endmodule

module IFID (
  input  clk,
  input  rst,
  input  en,
  input  [31:0] PC,
  input  [31:0] in_5,
  output [31:0] out_6,
  output [31:0] Instruction
);

  Register #(.width(32)) register_1 (.D(PC), .en(en), .Q(out_6), .clk(clk), .clr(rst));
  Register #(.width(32)) register_2 (.D(in_5), .en(en), .Q(Instruction), .clk(clk), .clr(rst));
endmodule

module IDEX (
  input  clk,
  input  rst,
  input  [31:0] PC,
  input  RegWrite,
  input  MemtoReg,
  input  [31:0] in_6,
  input  Branch,
  input  [31:0] ReadData2,
  input  MemWrite,
  input  [31:0] in_10,
  input  in_11,
  input  [31:0] Instruction,
  input  ALUSrc,
  input  [4:0] Rd,
  input  [4:0] in_15,
  input  [4:0] in_16,
  input  [4:0] in_17,
  output [31:0] out_18,
  output out_19,
  output out_20,
  output [31:0] ReadData1,
  output out_22,
  output [31:0] out_23,
  output out_24,
  output [31:0] Immediate,
  output MemRead,
  output [31:0] out_27,
  output out_28,
  output [4:0] out_29,
  output [4:0] ALUOp,
  output [4:0] ReadDir1,
  output [4:0] ReadDir2
);

  Register #(.width(32)) register_1 (.D(PC), .Q(out_18), .clk(clk), .clr(rst));  // open: en
  Register #(.width(32)) register_2 (.D(in_6), .Q(ReadData1), .clk(clk), .clr(rst));  // open: en
  Register #(.width(32)) register_3 (.D(ReadData2), .Q(out_23), .clk(clk), .clr(rst));  // open: en
  Register #(.width(32)) register_4 (.D(in_10), .Q(Immediate), .clk(clk), .clr(rst));  // open: en
  Register #(.width(32)) register_5 (.D(Instruction), .Q(out_27), .clk(clk), .clr(rst));  // open: en
  Register #(.width(5)) register_6 (.D(Rd), .Q(out_29), .clk(clk), .clr(rst));  // open: en
  Register #(.width(5)) register_7 (.D(in_16), .Q(ReadDir1), .clk(clk), .clr(rst));  // open: en
  Register #(.width(5)) register_8 (.D(in_17), .Q(ReadDir2), .clk(clk), .clr(rst));  // open: en
  Register #(.width(1)) register_9 (.D(RegWrite), .Q(out_19), .clk(clk), .clr(rst));  // open: en
  Register #(.width(1)) register_10 (.D(MemtoReg), .Q(out_20), .clk(clk), .clr(rst));  // open: en
  Register #(.width(1)) register_11 (.D(Branch), .Q(out_22), .clk(clk), .clr(rst));  // open: en
  Register #(.width(1)) register_12 (.D(MemWrite), .Q(out_24), .clk(clk), .clr(rst));  // open: en
  Register #(.width(1)) register_13 (.D(in_11), .Q(MemRead), .clk(clk), .clr(rst));  // open: en
  Register #(.width(1)) register_14 (.D(ALUSrc), .Q(out_28), .clk(clk), .clr(rst));  // open: en
  Register #(.width(5)) register_15 (.D(in_15), .Q(ALUOp), .clk(clk), .clr(rst));  // open: en

  // Notes on the sheet:
  //   DATAPATH
  //   FORWARDING
  //   CONTROL
  //   WB
  //   MEM
  //   EX
endmodule

module EXMEM (
  input  clk,
  input  rst,
  input  [31:0] in_3,
  input  in_4,
  input  in_5,
  input  in_6,
  input  [31:0] ALUOutput,
  input  Branch,
  input  in_9,
  input  [31:0] ReadData2,
  input  MemRead,
  input  [4:0] in_12,
  output [31:0] PCBranch,
  output RegWrite,
  output MemtoReg,
  output Zero,
  output [31:0] out_17,
  output out_18,
  output MemWrite,
  output [31:0] out_20,
  output out_21,
  output [4:0] Rd
);

  Register #(.width(32)) register_1 (.D(in_3), .Q(PCBranch), .clk(clk), .clr(rst));  // open: en
  Register #(.width(1)) register_2 (.D(in_6), .Q(Zero), .clk(clk), .clr(rst));  // open: en
  Register #(.width(32)) register_3 (.D(ALUOutput), .Q(out_17), .clk(clk), .clr(rst));  // open: en
  Register #(.width(32)) register_4 (.D(ReadData2), .Q(out_20), .clk(clk), .clr(rst));  // open: en
  Register #(.width(5)) register_5 (.D(in_12), .Q(Rd), .clk(clk), .clr(rst));  // open: en
  Register #(.width(1)) register_6 (.D(in_4), .Q(RegWrite), .clk(clk), .clr(rst));  // open: en
  Register #(.width(1)) register_7 (.D(in_5), .Q(MemtoReg), .clk(clk), .clr(rst));  // open: en
  Register #(.width(1)) register_8 (.D(Branch), .Q(out_18), .clk(clk), .clr(rst));  // open: en
  Register #(.width(1)) register_9 (.D(in_9), .Q(MemWrite), .clk(clk), .clr(rst));  // open: en
  Register #(.width(1)) register_10 (.D(MemRead), .Q(out_21), .clk(clk), .clr(rst));  // open: en

  // Notes on the sheet:
  //   DATAPATH
  //   CONTROL
  //   WB
  //   MEM
endmodule

module MEMWB (
  input  clk,
  input  rst,
  input  [31:0] ALUOutput,
  input  in_4,
  input  MemtoReg,
  input  [31:0] in_6,
  input  [4:0] in_7,
  output [31:0] out_8,
  output RegWrite,
  output out_10,
  output [31:0] DataOutput,
  output [4:0] WriteDir
);

  Register #(.width(32)) register_1 (.D(ALUOutput), .Q(out_8), .clk(clk), .clr(rst));  // open: en
  Register #(.width(32)) register_2 (.D(in_6), .Q(DataOutput), .clk(clk), .clr(rst));  // open: en
  Register #(.width(5)) register_3 (.D(in_7), .Q(WriteDir), .clk(clk), .clr(rst));  // open: en
  Register #(.width(1)) register_4 (.D(in_4), .Q(RegWrite), .clk(clk), .clr(rst));  // open: en
  Register #(.width(1)) register_5 (.D(MemtoReg), .Q(out_10), .clk(clk), .clr(rst));  // open: en

  // Notes on the sheet:
  //   DATAPATH
  //   CONTROL
  //   WB
endmodule

module Forwarding (
  input  [4:0] Rs1,
  input  [4:0] Rs2,
  input  [4:0] MEMRd,
  input  [4:0] WBRd,
  input  RegWriteMEM,
  input  RegWrite,
  input  ALUSrc,
  output [1:0] ForwardA,
  output [1:0] ForwardB
);
endmodule

module HazardDetection (
  input  [31:0] Instruction,
  input  MemReadID,
  input  MemReadEX,
  input  BranchID,
  input  [4:0] EXRd,
  input  PCSrc,
  output PCWrite,
  output IFIDWrite,
  output Stall,
  output IFIDFlush
);


  // Notes on the sheet:
  //   STALL
  //   FLUSH
  //   ALU Stall
  //   Branch Stall: RTYPE or LOAD
  //   ALU depends on load data, stall for one cycle using MemReadEX
  //   Uses both MemRead to stall 2 cycles for a load, then forwarding.
  //   La idea es implementar la instrucción nop y en el caso de que se deba producir una bubble, detener la escritura ENABLE del PC y IFIDreg y sustituir la instrucción por un NOP
  //   Mala opción usar un nop como stall. Razón word bibliografía.
  //   STALL
  //   FLUSH
endmodule

// VHDL entity MainControlVHDL, as the project stores it:
--------------------------------------------------------------------------------
-- Project :
-- File    :
-- Autor   :
-- Date    :
--
--------------------------------------------------------------------------------
-- Description :
--
--------------------------------------------------------------------------------

LIBRARY ieee;
USE ieee.std_logic_1164.all;

ENTITY MainControlVHDL IS
  PORT (
  ------------------------------------------------------------------------------
  --Insert input ports below
    clock      : IN  std_logic;                    -- input bit example
    val        : IN  std_logic_vector(3 DOWNTO 0); -- input vector example
  ------------------------------------------------------------------------------
  --Insert output ports below
    max        : OUT std_logic;                    -- output bit example
    cpt        : OUT std_logic_vector(3 DOWNTO 0)  -- output vector example
    );
END MainControlVHDL;

--------------------------------------------------------------------------------
--Complete your VHDL description below
--------------------------------------------------------------------------------

ARCHITECTURE TypeArchitecture OF MainControlVHDL IS

BEGIN


END TypeArchitecture;
